// Logisim project semaforo.circ as structural Verilog: 6 circuits, main circuit ControladorA
module main (
);

  wire a0, a1, AmareloA, AmareloB, and_1_out, b0, b1, button_1_out, clock_1_out, d_ff_1_q, d_ff_2_q,
       detectavermelho_1_s0, s_r_ff_1_q, transistor_1_out, verdeA, verdeB, VermelhoA, VermelhoB;

  Clock clock_1 (.out(clock_1_out));
  Transistor transistor_1 (.in(clock_1_out), .out(transistor_1_out), .gate(d_ff_1_q));
  SemafaroA semafaroa_1 (
    .e1(a1), .e0(a0), .S_vermelho(d_ff_1_q), .verde(verdeA), .amarelo(AmareloA), .vermelho(VermelhoA));
  ControladorA controladora_1 (.Clock(transistor_1_out), .s1(a1), .s0(a0));
  ControladorB controladorb_1 (.clock(transistor_1_out), .out_2(b1), .out_3(b0));
  SemaforoB semaforob_1 (
    .e1(b1), .e0(b0), .seta_vermelho(d_ff_1_q), .verde(verdeB), .amarelo(AmareloB), .vermelho(VermelhoB));
  LED led_1 (.in(verdeA));
  LED led_2 (.in(AmareloA));
  LED led_3 (.in(VermelhoA));
  LED led_4 (.in(VermelhoB));
  LED led_5 (.in(AmareloB));
  LED led_6 (.in(verdeB));
  LED led_7 (.in(d_ff_1_q));
  LED led_8 (.in(verdeA));
  LED led_9 (.in(AmareloA));
  LED led_10 (.in(VermelhoA));
  LED led_11 (.in(d_ff_1_q));
  Button button_1 (.out(button_1_out));
  D_Flip_Flop d_ff_1 (.D(and_1_out), .clk(clock_1_out), .Q(d_ff_1_q));  // open: Qn, preset, reset
  S_R_Flip_Flop #(.trigger("high")) s_r_ff_1 (
    .S(button_1_out), .R(d_ff_2_q), .clk(1'b1), .Q(s_r_ff_1_q));  // open: reset, Qn, preset
  DetectaVermelho detectavermelho_1 (.a1(a1), .a0(a0), .b1(b1), .b0(b0), .s0(detectavermelho_1_s0));
  and and_1 (and_1_out, s_r_ff_1_q, detectavermelho_1_s0);
  D_Flip_Flop d_ff_2 (.D(and_1_out), .clk(clock_1_out), .Q(d_ff_2_q));  // open: Qn, preset, reset
endmodule

module ControladorA (
  input  Clock,
  output s1,
  output s0
);

  wire and_1_out, and_2_out, ff0_q, ff0_qn, ff1_qn, not_1_out, not_2_out, or_1_out;

  not not_1 (not_1_out, s1);
  not not_2 (not_2_out, ff0_q);
  and and_1 (and_1_out, not_1_out, ff0_q);
  and and_2 (and_2_out, s1, not_2_out);
  or or_1 (or_1_out, and_1_out, and_2_out);
  D_Flip_Flop ff1 (.D(or_1_out), .clk(Clock), .Q(s1), .Qn(ff1_qn));  // open: preset, reset
  D_Flip_Flop ff0 (.D(ff0_qn), .clk(Clock), .Q(ff0_q), .Qn(ff0_qn));  // open: preset, reset
  and and_3 (s0, ff1_qn, ff0_q);

  // Other names for the same wires on the sheet: ff1_q = s1
endmodule

module ControladorB (
  input  clock,
  output out_2,
  output out_3
);

  wire and_1_out, and_2_out, ff0_q, ff0_qn, not_1_out, not_2_out, or_1_out;

  not not_1 (not_1_out, out_2);
  not not_2 (not_2_out, ff0_q);
  and and_1 (and_1_out, not_1_out, ff0_q);
  and and_2 (and_2_out, out_2, not_2_out);
  or or_1 (or_1_out, and_1_out, and_2_out);
  D_Flip_Flop ff1 (.D(or_1_out), .clk(clock), .Q(out_2));  // open: Qn, preset, reset
  D_Flip_Flop ff0 (.D(ff0_qn), .clk(clock), .Q(ff0_q), .Qn(ff0_qn));  // open: preset, reset
  and and_3 (out_3, out_2, ff0_q);

  // Other names for the same wires on the sheet: ff1_q = out_2
endmodule

module DetectaVermelho (
  input  a1,
  input  a0,
  input  b1,
  input  b0,
  output s0
);

  wire and_1_out, and_2_out, not_1_out, not_2_out;

  not not_1 (not_1_out, a1);
  not not_2 (not_2_out, b1);
  and and_1 (and_1_out, not_1_out, a0, not_2_out);
  and and_2 (and_2_out, a1, b1, b0);
  or or_1 (s0, and_1_out, and_2_out);
endmodule

module SemafaroA (
  input  e1,
  input  e0,
  input  S_vermelho,
  output verde,
  output amarelo,
  output vermelho
);

  wire not_1_out, not_2_out, not_3_out;

  not not_1 (not_1_out, e1);
  not not_2 (not_2_out, e0);
  not not_3 (not_3_out, S_vermelho);
  and and_1 (verde, not_1_out, not_2_out, not_3_out);
  and and_2 (amarelo, not_1_out, e0, not_3_out);
  or or_1 (vermelho, e1, S_vermelho);
endmodule

module SemaforoB (
  input  e1,
  input  e0,
  input  seta_vermelho,
  output verde,
  output amarelo,
  output vermelho
);

  wire not_1_out, not_2_out, not_3_out;

  not not_1 (not_1_out, seta_vermelho);
  not not_2 (not_2_out, e0);
  not not_3 (not_3_out, e1);
  and and_1 (verde, not_1_out, e1, not_2_out);
  and and_2 (amarelo, not_1_out, e0);
  or or_1 (vermelho, seta_vermelho, not_3_out);
endmodule
